// Logisim project FinalProject1.circ as structural Verilog
module main (
  output LED9,
  output LED8,
  output LED7,
  output LED6,
  output Ta,
  output Tb,
  output Tc,
  output Td,
  output Te,
  output Tf,
  output Tg,
  output Oa,
  output Ob,
  output Oc,
  output Od,
  output Oe,
  output ONEf,
  output Og
);

  wire AG, AR, AY, BG, BR, BY, CLK, not_1_out, not_2_out, NS_n0, NS_n1, NS_n2, PedestrianA_out,
       PedestrianB_out, Q0, Q1, Q2, Req_req, T_step;
  wire [3:0] ONES, t, TENS;

  Clock clock_1 (.out(CLK));
  LED u_AG (.in(AG));
  LED u_AY (.in(AY));
  LED u_AR (.in(AR));
  Hex_Digit_Display D2 (.value(TENS));  // open: dp
  Button PedestrianA (.out(PedestrianA_out));
  Button PedestrianB (.out(PedestrianB_out));
  Hex_Digit_Display D1 (.value(ONES));  // open: dp
  not not_1 (not_1_out, PedestrianA_out);
  not not_2 (not_2_out, PedestrianB_out);
  LED u_BG (.in(BG));
  LED u_BY (.in(BY));
  LED u_BR (.in(BR));
  Request Req (.PedA(not_1_out), .PedB(not_2_out), .W(Q2), .CLK(CLK), .REQ(Req_req));
  NextState NS (.Q2(Q2), .Q1(Q1), .Q0(Q0), .R(Req_req), .N2(NS_n2), .N1(NS_n1), .N0(NS_n0));
  Timer u_T (.CLK(CLK), .Q2(Q2), .Q1(Q1), .t(t), .STEP(T_step));
  DispLogic DL (.Q2(Q2), .t(t), .TENS(TENS), .ONES(ONES));
  StateReg SR (.CLK(CLK), .N2(NS_n2), .N1(NS_n1), .N0(NS_n0), .STEP(T_step), .Q2(Q2), .Q1(Q1), .Q0(Q0));
  SegDecod Hex1 (
    .D3(TENS[3]), .D2(TENS[2]), .D1(TENS[1]), .D0(TENS[0]), .a(Ta), .b(Tb), .c(Tc), .d(Td), .e(Te), .f(Tf),
    .g(Tg));
  SegDecod Hex0 (
    .D3(ONES[3]), .D2(ONES[2]), .D1(ONES[1]), .D0(ONES[0]), .a(Oa), .b(Ob), .c(Oc), .d(Od), .e(Oe), .f(ONEf),
    .g(Og));
  OutLogic OL (.Q2(Q2), .Q1(Q1), .Q0(Q0), .AR(AR), .AY(AY), .AG(AG), .BR(BR), .BY(BY), .BG(BG));

  assign LED6 = 1'b0;
  assign LED7 = 1'b0;
  assign LED8 = 1'b0;
  assign LED9 = 1'b0;
endmodule

module Request (
  input  PedA,
  input  PedB,
  input  W,
  input  CLK,
  output REQ
);

  wire and_1_out, not_1_out, or_1_out;

  or or_1 (or_1_out, PedA, PedB);
  not not_1 (not_1_out, W);
  and and_1 (and_1_out, or_1_out, not_1_out);
  D_Flip_Flop d_ff_1 (.D(REQ), .clk(CLK), .Q(REQ), .preset(and_1_out), .reset(W));  // open: Qn
endmodule

module NextState (
  input  Q2,
  input  Q1,
  input  Q0,
  input  R,
  output N2,
  output N1,
  output N0
);

  wire and_1_out, and_2_out, and_3_out, nor_1_out, not_1_out, not_2_out, not_3_out, not_4_out, not_5_out,
       not_6_out, xor_1_out;

  not not_1 (not_1_out, Q2);
  not not_2 (not_2_out, Q1);
  not not_3 (not_3_out, R);
  not not_4 (not_4_out, Q0);
  xor xor_1 (xor_1_out, Q2, Q1);
  and and_1 (and_1_out, not_1_out, not_2_out, Q0, not_3_out);
  not not_5 (not_5_out, Q2);
  and and_2 (and_2_out, not_5_out, Q1, R);
  not not_6 (not_6_out, Q2);
  and and_3 (and_3_out, not_4_out, xor_1_out);
  nor nor_1 (nor_1_out, Q2, Q0);
  and and_4 (N2, not_6_out, Q0, R);
  or or_1 (N1, and_3_out, and_1_out);
  or or_2 (N0, nor_1_out, and_2_out);
endmodule

module StateReg (
  input  CLK,
  input  N2,
  input  N1,
  input  N0,
  input  STEP,
  output Q2,
  output Q1,
  output Q0
);

  wire D0, D1, D2;

  D_Flip_Flop d_ff_1 (.D(D2), .clk(CLK), .Q(Q2));  // open: Qn, preset, reset
  Multiplexer multiplexer_1 (.in0(Q2), .in1(N2), .out(D2), .sel(STEP));
  Multiplexer multiplexer_2 (.in0(Q1), .in1(N1), .out(D1), .sel(STEP));
  D_Flip_Flop d_ff_2 (.D(D1), .clk(CLK), .Q(Q1));  // open: Qn, preset, reset
  Multiplexer multiplexer_3 (.in0(Q0), .in1(N0), .out(D0), .sel(STEP));
  D_Flip_Flop d_ff_3 (.D(D0), .clk(CLK), .Q(Q0));  // open: Qn, preset, reset
endmodule

module OutLogic (
  input  Q2,
  input  Q1,
  input  Q0,
  output AR,
  output AY,
  output AG,
  output BR,
  output BY,
  output BG
);

  wire not_1_out, not_2_out, not_3_out, not_4_out, not_5_out, not_6_out;

  not not_1 (not_1_out, Q2);
  not not_2 (not_2_out, Q1);
  not not_3 (not_3_out, Q2);
  not not_4 (not_4_out, Q2);
  not not_5 (not_5_out, Q0);
  or or_1 (AR, Q2, Q1);
  not not_6 (not_6_out, Q1);
  and and_1 (AY, not_1_out, not_6_out, Q0);
  nor nor_1 (AG, Q2, Q1, Q0);
  or or_2 (BR, not_2_out, Q2);
  and and_2 (BY, not_3_out, Q1, Q0);
  and and_3 (BG, not_4_out, Q1, not_5_out);
endmodule

module Timer (
  input  CLK,
  input  Q2,
  input  Q1,
  output [3:0] t,
  output STEP
);

  wire and_1_out, comparator_1_eq, comparator_2_eq, multiplexer_2_out;
  wire [3:0] adder_1_out, multiplexer_1_out;

  Multiplexer #(.width(4)) multiplexer_1 (.in0(adder_1_out), .in1(4'b0000), .out(multiplexer_1_out), .sel(STEP));
  Register #(.width(4)) register_1 (.D(multiplexer_1_out), .en(1'b1), .clk(CLK), .Q(t));  // open: clr
  and and_1 (and_1_out, Q2, Q1);
  Adder #(.width(4)) adder_1 (.a(4'b0001), .b(t), .out(adder_1_out));  // open: cin, cout
  Comparator #(.width(4)) comparator_1 (.a(t), .b(4'b0010), .eq(comparator_1_eq));  // open: gt, lt
  Comparator #(.width(4)) comparator_2 (.a(t), .b(4'b1001), .eq(comparator_2_eq));  // open: gt, lt
  Multiplexer multiplexer_2 (.in0(comparator_1_eq), .in1(comparator_2_eq), .out(multiplexer_2_out), .sel(Q2));
  or or_1 (STEP, multiplexer_2_out, and_1_out);
endmodule

module DispLogic (
  input  Q2,
  input  [3:0] t,
  output [3:0] TENS,
  output [3:0] ONES
);

  wire MBS;
  wire [3:0] multiplexer_1_out, subtractor_1_out;

  Multiplexer #(.width(4)) multiplexer_1 (.in0(4'b0011), .in1(4'b1010), .out(multiplexer_1_out), .sel(Q2));
  Subtractor #(.width(4)) subtractor_1 (.a(multiplexer_1_out), .b(t), .out(subtractor_1_out));  // open: bin, bout
  Comparator #(.width(4)) comparator_1 (.a(subtractor_1_out), .b(4'b1010), .eq(MBS));  // open: gt, lt
  Multiplexer #(.width(4)) multiplexer_2 (.in0(subtractor_1_out), .in1(4'b0000), .out(ONES), .sel(MBS));
  assign TENS = {{3{1'b0}}, MBS};  // Bit_Extender bit_extender_1
endmodule

module SegDecod (
  input  D3,
  input  D2,
  input  D1,
  input  D0,
  output a,
  output b,
  output c,
  output d,
  output e,
  output f,
  output g
);

  wire and_1_out, and_2_out, and_3_out, and_4_out, and_5_out, and_6_out, and_7_out, and_8_out, and_9_out,
       and_10_out, and_11_out, and_12_out, and_13_out, and_14_out, and_15_out, and_16_out, and_17_out,
       and_18_out, and_19_out, and_20_out, and_21_out, and_22_out, and_23_out, and_24_out, and_25_out,
       and_26_out, not_1_out, not_2_out, not_3_out, not_4_out;

  not not_1 (not_1_out, D3);
  not not_2 (not_2_out, D2);
  not not_3 (not_3_out, D1);
  not not_4 (not_4_out, D0);
  and and_1 (and_1_out, not_1_out, not_2_out, not_3_out, D0);
  and and_2 (and_2_out, D2, not_3_out, not_4_out);
  and and_3 (and_3_out, D3, D1);
  and and_4 (and_4_out, D3, D2);
  and and_5 (and_5_out, D2, not_3_out, D0);
  and and_6 (and_6_out, D2, D1, not_4_out);
  and and_7 (and_7_out, D3, D1);
  and and_8 (and_8_out, D3, D2);
  and and_9 (and_9_out, not_2_out, D1, not_4_out);
  and and_10 (and_10_out, D3, D1);
  and and_11 (and_11_out, D3, D2);
  and and_12 (and_12_out, not_1_out, not_2_out, not_3_out, D0);
  and and_13 (and_13_out, D2, not_3_out, not_4_out);
  and and_14 (and_14_out, D2, D1, D0);
  and and_15 (and_15_out, D3, D1);
  and and_16 (and_16_out, D3, D2);
  and and_17 (and_17_out, D2, not_3_out);
  and and_18 (and_18_out, D3, D1);
  and and_19 (and_19_out, not_1_out, not_2_out, D0);
  and and_20 (and_20_out, not_2_out, D1);
  and and_21 (and_21_out, D1, D0);
  and and_22 (and_22_out, D3, D2);
  and and_23 (and_23_out, not_1_out, not_2_out, not_3_out);
  and and_24 (and_24_out, D2, D1, D0);
  and and_25 (and_25_out, D3, D1);
  and and_26 (and_26_out, D3, D2);
  or or_1 (a, and_1_out, and_2_out, and_3_out, and_4_out);
  or or_2 (b, and_5_out, and_6_out, and_7_out, and_8_out);
  or or_3 (c, and_9_out, and_10_out, and_11_out);
  or or_4 (d, and_12_out, and_13_out, and_14_out, and_15_out, and_16_out);
  or or_5 (e, D0, and_17_out, and_18_out);
  or or_6 (f, and_19_out, and_20_out, and_21_out, and_22_out);
  or or_7 (g, and_23_out, and_24_out, and_25_out, and_26_out);
endmodule
