// Logisim project FPGAboardsetup.circ as structural Verilog: 1 circuit, main circuit main
module main (
  input  Input_1,
  input  Input_2,
  output Output_1,
  output Output_2
);


  assign Output_1 = Input_1;
  assign Output_2 = Input_2;
endmodule
