// Logisim project Fulladder10.6.circ as structural Verilog: 1 circuit, main circuit main
module main (
  input  Input_1,
  input  Input_2,
  input  Input_3,
  output Output_1,
  output Output_2
);

  wire and_1_out, and_2_out, xor_1_out;

  xor xor_1 (xor_1_out, Input_1, Input_2);
  xor xor_2 (Output_1, xor_1_out, Input_3);
  and and_1 (and_1_out, Input_3, xor_1_out);
  and and_2 (and_2_out, Input_2, Input_1);
  or or_1 (Output_2, and_1_out, and_2_out);
endmodule
